# Fritzing sketch NodeMcuHandle (saved by Fritzing 0.9.3b)
breadboards: 1

parts:
  U1 = NodeMCU V1.0
  R1 = Resistor [tolerance=±5% resistance=220 package=THT]
  S1 = Pushbutton [package="[THT]"]
  S2 = Pushbutton [package="[THT]"]
  S3 = Pushbutton [package="[THT]"]
  S4 = Pushbutton [package="[THT]"]
  R2 = Resistor [tolerance=±5% resistance=220 package=THT]
  R3 = Resistor [tolerance=±5% resistance=220 package=THT]
  R4 = Resistor [tolerance=±5% resistance=220 package=THT]

nets:
  N1: U1.3V3, S1.Pin_3, S1.Pin_4, S2.Pin_3, S2.Pin_4, S3.Pin_3, S3.Pin_4, S4.Pin_3, S4.Pin_4
  N2: U1.GND, R1.Pin_1, R2.Pin_1, R3.Pin_1, R4.Pin_1
  N3: U1.D5, R1.Pin_0, S2.Pin_1, S2.Pin_2
  N4: U1.D6, S1.Pin_1, S1.Pin_2, R2.Pin_0
  N5: U1.D7, S4.Pin_1, S4.Pin_2, R3.Pin_0
  N6: U1.D8, S3.Pin_1, S3.Pin_2, R4.Pin_0

custom parts:
  NodeMCU V1.0: ESP8266 based NodeMCU
